# Fritzing sketch MCButtonsAND (saved by Fritzing 0.8.3b)
breadboards: 1

parts:
  S1 = Momentary Switch [package=ksa_sealed_tac_switch]
  S2 = Momentary Switch [package=ksa_sealed_tac_switch]
  R1 = Resistor [tolerance=±5% resistance=220 package=THT]
  VCC1 = 4 x AAA Battery Mount
  LED1 = LED - 5mm [color="Red (633nm)" package="5 mm [THT]"]

nets:
  N1: S1.2, S2.4
  N2: S1.4, VCC1.+
  N3: S2.2, R1.Pin_0
  N4: R1.Pin_1, LED1.cathode
  N5: VCC1.-, LED1.anode
