# Fritzing sketch MCButtonsOR (saved by Fritzing 0.8.3b)
breadboards: 1

parts:
  S1 = Momentary Switch [package=ksa_sealed_tac_switch]
  S2 = Momentary Switch [package=ksa_sealed_tac_switch]
  R1 = Resistor [tolerance=±5% resistance=220 package=THT]
  LED1 = LED - 5mm [color="Red (633nm)" package="5 mm [THT]"]
  VCC1 = 4 x AAA Battery Mount

nets:
  N1: S1.2, S2.2, R1.Pin_0
  N2: S1.4, S2.4, VCC1.+
  N3: R1.Pin_1, LED1.cathode
  N4: LED1.anode, VCC1.-
