# Fritzing sketch MinecraftRLANDgate (saved by Fritzing 0.7.12b)
breadboards: 1

parts:
  Q1 = NPN-Transistor [package="TO92 [THT]"]
  Q2 = NPN-Transistor [package="TO92 [THT]"]
  R1 = Resistor [tolerance=±5% resistance=10k package=THT]
  R2 = Resistor [tolerance=±5% resistance=10k package=THT]
  R3 = Resistor [tolerance=±5% resistance=4.7k package=THT]
  LED1 = LED - 5mm [color="Red (633nm)" package="5 mm [THT]"]
  S1 = Pushbutton [package="[THT]"]
  S2 = Pushbutton [package="[THT]"]

nets:
  N1: Q1.E, R3.Pin_1
  N2: Q1.B, R1.Pin_1
  N3: Q1.C, Q2.E
  N4: Q2.B, R2.Pin_1
  N5: R1.Pin_0, S1.Pin_1, S1.Pin_2
  N6: R2.Pin_0, S2.Pin_1, S2.Pin_2
  N7: R3.Pin_0, LED1.anode
  N8: S1.Pin_3, S1.Pin_4
  N9: S2.Pin_3, S2.Pin_4
