# Fritzing sketch MinecraftRLORgate (saved by Fritzing 0.7.12b)
breadboards: 1

parts:
  VCC1 = 4 x AAA Battery Mount
  Q1 = NPN-Transistor [package="TO92 [THT]"]
  Q2 = NPN-Transistor [package="TO92 [THT]"]
  R1 = Resistor [tolerance=±5% resistance=10k package=THT]
  R2 = Resistor [tolerance=±5% resistance=10k package=THT]
  LED1 = LED - 5mm [color="Red (633nm)" package="5 mm [THT]"]
  R3 = Resistor [tolerance=±5% resistance=220 package=THT]
  R4 = Resistor [tolerance=±5% resistance=220 package=THT]  # not connected
  R5 = Resistor [tolerance=±5% resistance=220 package=THT]

nets:
  N1: VCC1.-, R3.Pin_0
  N2: VCC1.+, Q1.C, Q2.C
  N3: Q1.E, Q2.E, R5.Pin_1
  GND: Q1.B, R1.Pin_1, LED1.cathode, R3.Pin_1
  N4: Q2.B, R2.Pin_1
  N5: LED1.anode, R5.Pin_0
